# Fritzing sketch Rasp_IO_2LED_1SW (saved by Fritzing 0.9.3b)
breadboards: 1

parts:
  Raspberry_Pi_1 = Raspberry Pi 3 [part_number=RPI-3-V1.2]
  LED2 = LED - 5mm [color="Green (560nm)" package="5 mm [THT]"]
  R1 = Resistor [tolerance=±5% resistance=1k package=THT]
  S1 = Pushbutton [package="[THT]"]
  LED1 = LED - 3mm [color="Orange (612nm)" package="3 mm [THT]"]
  R3 = Resistor [tolerance=±5% resistance=470 package=THT]
  R4 = Resistor [tolerance=±5% resistance=470 package=THT]
  R2 = Resistor [tolerance=±5% resistance=10k package=THT]

nets:
  N1: Raspberry_Pi_1.3v3, S1.Pin_1, S1.Pin_2
  N2: Raspberry_Pi_1.GIPO4, R1.Pin_0
  N3: Raspberry_Pi_1.GIPO5, LED2.anode
  N4: Raspberry_Pi_1.GIPO6, LED1.anode
  N5: Raspberry_Pi_1.GND, R3.Pin_0, R4.Pin_0, R2.Pin_1
  N6: LED2.cathode, R3.Pin_1
  N7: R1.Pin_1, S1.Pin_3, S1.Pin_4, R2.Pin_0
  N8: LED1.cathode, R4.Pin_1

notes:
  3.3V PWR
  GPIO 4
  GPIO 5
  GPIO 6
  GND
